# Fritzing sketch at-me - laerdal (saved by Fritzing 0.9.5d)
circuit board: 5.47364cm x 5.5411cm
circuit board: 2.28753cm x 2.69625cm
circuit board: 2.17311cm x 1.67921cm
perfboards: 6

parts:
  Arduino_Nano = Arduino Nano (Rev3.0)
  DFRobot_DFPlayer_Mini1 = DFRobot DFPlayer Mini [part_number=DFR0299]
  R12 = Resistor [tolerance=±5% resistance=1k package=THT]
  R2 = Resistor [tolerance=±5% resistance=220 package=THT]
  R5 = Resistor [tolerance=±5% resistance=220 package=THT]
  R4 = Resistor [tolerance=±5% resistance=10k package=THT]
  Speakers = female pin header, 2 pins [form="♀ (female)"]
  LED_Pads_Out = female pin header, 2 pins [form="♀ (female)"]
  LED_Shock = female pin header, 2 pins [form="♀ (female)"]
  Pads_Out = female pin header, 2 pins [form="♀ (female)"]
  Shock_Deliver = female pin header, 2 pins [form="♀ (female)"]
  Poweron = female pin header, 2 pins [form="♀ (female)"]
  LED_Poweron_Out = female pin header, 2 pins [form="♀ (female)"]
  R10 = Resistor [tolerance=±5% resistance=220 package=THT]
  R3 = Resistor [tolerance=±5% resistance=10k package=THT]
  SpeakerIn = female pin header, 2 pins [form="♀ (female)"]
  SpeakOut = rounded female pin header, 2 pins [form="♀ (female rounded)"]
  Shock_Deliver_Led_In = female pin header, 2 pins [form="♀ (female)"]
  Shock_Deliever_Button = Pushbutton [package="[THT]"]
  Shock_Deliever_Button_In = female pin header, 2 pins [form="♀ (female)"]
  SP1 = SPEAKER [package=pcb_mount_speaker]
  Power_Led_In = female pin header, 2 pins [form="♀ (female)"]
  PowerOn_In = female pin header, 2 pins [form="♀ (female)"]
  PowerOn_Button = Pushbutton [package="[THT]"]
  J1 = female pin header, 2 pins [form="♀ (female)"]
  Pads_Button_In = female pin header, 2 pins [form="♀ (female)"]
  S1 = Pushbutton [package="[THT]"]
  LED1 = LED - 3mm [color="Yellow (595nm)" package="3 mm [THT]"]
  Power_LED = LED - 3mm [color="Red (635nm)" package="3 mm [THT]"]
  LED2 = LED - 3mm [color="Orange (620nm)" package="3 mm [THT]"]
  PowerSupply_LED = LED - 3mm [color="Infrared (880nm)" package="3 mm [THT]"]  # not connected
  YwRobot_Power_Supply1 = YwRobot Breadboard Power Supply [part_number=545043]  # not connected

nets:
  N1: Arduino_Nano.GND, DFRobot_DFPlayer_Mini1.GND-1, DFRobot_DFPlayer_Mini1.GND-2, R4.Pin_0, LED_Pads_Out.pin2, LED_Shock.pin2, Poweron.pin2, LED_Poweron_Out.pin1, R3.Pin_1, Shock_Deliver_Led_In.pin1, Power_Led_In.pin1, PowerOn_In.pin1, PowerOn_Button.Pin_3, PowerOn_Button.Pin_4, J1.pin2, LED1.cathode, Power_LED.cathode, LED2.cathode
  N2: Arduino_Nano.D2, R2.Pin_0
  N3: Arduino_Nano.D3, Pads_Out.pin2, R3.Pin_0, Pads_Button_In.pin1, S1.Pin_3, S1.Pin_4
  N4: Arduino_Nano.D4, R4.Pin_1, Shock_Deliver.pin2, Shock_Deliever_Button.Pin_1, Shock_Deliever_Button.Pin_2, Shock_Deliever_Button_In.pin2
  N5: Arduino_Nano.D5, R5.Pin_0
  N6: Arduino_Nano.D6, Poweron.pin1, PowerOn_In.pin2, PowerOn_Button.Pin_1, PowerOn_Button.Pin_2
  N7: Arduino_Nano.D7, R10.Pin_1
  N8: Arduino_Nano.D8, DFRobot_DFPlayer_Mini1.TX
  N9: Arduino_Nano.D12/MISO, R12.Pin_1
  5V: Arduino_Nano.5V, DFRobot_DFPlayer_Mini1.VCC, Pads_Out.pin1, Shock_Deliver.pin1, Shock_Deliever_Button.Pin_3, Shock_Deliever_Button.Pin_4, Shock_Deliever_Button_In.pin1, Pads_Button_In.pin2, S1.Pin_1, S1.Pin_2
  N10: DFRobot_DFPlayer_Mini1.RX, R12.Pin_0
  N11: DFRobot_DFPlayer_Mini1.SPK_1, Speakers.pin1, SpeakerIn.pin2, SpeakOut.pin2, SP1.+
  N12: DFRobot_DFPlayer_Mini1.SPK_2, Speakers.pin2, SpeakerIn.pin1, SpeakOut.pin1, SP1.-
  N13: R2.Pin_1, LED_Pads_Out.pin1, J1.pin1, LED1.anode
  N14: R5.Pin_1, LED_Shock.pin1, Shock_Deliver_Led_In.pin2, LED2.anode
  N15: LED_Poweron_Out.pin2, R10.Pin_0, Power_Led_In.pin2, Power_LED.anode

notes:
  AT-ME v.0.3

custom parts:
  YwRobot Breadboard Power Supply: The YwRobot Breadboard Power Supply (MB-V2) has two power rails; they can be 5V or 3V3. Power to the module can be provided through the female USB socket or through the A10 (female) 2.1mm power jack.
