# Fritzing sketch at-me-perfboard (saved by Fritzing 0.9.5d)
stripboards: 1

parts:
  Shock = Round Pushbutton
  J2 = female pin header, 2 pins [form="♀ (female)"]
  TRRS1 = Audio Jack (TRS) 3.5mm [package="4Ucon 08780 [THT]"]
  R7 = Resistor [tolerance=±5% resistance=220 package=THT]
  LED5 = LED - 5mm [color="Red (633nm)" package="5 mm [THT]"]
  R8 = Resistor [tolerance=±5% resistance=220 package=THT]
  LED6 = smd LED [color="Yellow (595nm)" package="1206 [SMD]"]
  R10 = Resistor [tolerance=±5% resistance=1k package=THT]
  Arduino_Nano1 = Arduino Nano (Rev3.0)
  DFRobot_DFPlayer_Mini2 = DFRobot DFPlayer Mini [part_number=DFR0299]
  Power = Round Pushbutton
  R3 = Resistor [tolerance=±5% resistance=10k package=THT]
  J3 = female pin header, 2 pins [form="♀ (female)"]
  J4 = female pin header, 2 pins [form="♀ (female)"]
  J5 = female pin header, 2 pins [form="♀ (female)"]
  J6 = female pin header, 2 pins [form="♀ (female)"]
  R11 = Resistor [tolerance=±5% resistance=10k package=THT]
  Pads = Screw terminal - 2 pins [package=THT]

nets:
  5V: Shock.leg0, J2.pin2, Arduino_Nano1.5V, DFRobot_DFPlayer_Mini2.VCC, J4.pin1, Pads.pin2
  N1: Shock.leg1, J2.pin1, Arduino_Nano1.D4, R11.Pin_0
  N2: TRRS1.Sleeve, DFRobot_DFPlayer_Mini2.SPK_2
  N3: TRRS1.Ring, TRRS1.Tip, DFRobot_DFPlayer_Mini2.SPK_1
  N4: R7.Pin_0, Arduino_Nano1.D5
  N5: R7.Pin_1, LED5.anode, J6.pin1
  N6: LED5.cathode, LED6.cathode, Arduino_Nano1.GND, DFRobot_DFPlayer_Mini2.GND-1, DFRobot_DFPlayer_Mini2.GND-2, Power.leg0, R3.Pin_1, J3.pin1, J5.pin1, J6.pin2, R11.Pin_1
  N7: R8.Pin_0, Arduino_Nano1.D2
  N8: R8.Pin_1, LED6.anode, J3.pin2
  N9: R10.Pin_0, DFRobot_DFPlayer_Mini2.RX
  N10: R10.Pin_1, Arduino_Nano1.D11/MOSI
  N11: Arduino_Nano1.D3, R3.Pin_0, J4.pin2, Pads.pin1
  N12: Arduino_Nano1.D6, Power.leg1, J5.pin2
  N13: Arduino_Nano1.D10, DFRobot_DFPlayer_Mini2.TX
